// Logisim project CPU 4 bits CC4M.circ as structural Verilog: 16 circuits, main circuit main
module main (
);

  wire button_1_out, clock_1_out, d_ff_1_q, d_ff_2_q, not_1_out, not_2_out, uc_1_ac, uc_1_e, uc_1_ir,
       uc_1_load, uc_1_pc, uc_1_ram, uc_1_rst_pc, uc_1_rw, ula_1_overflow, ula_1_zero;
  wire [2:0] uc_1_opcode;
  wire [3:0] ac_1_s, mux_1_s, PC_q, ram_1_data, uc_1_dados, uc_1_operando, ula_1_s;
  wire [7:0] ir_1_s, rom_1_data;

  not not_1 (not_1_out, uc_1_load);
  Counter #(.width(4), .max('hf)) PC (
    .load(uc_1_load), .D(uc_1_dados), .count(not_1_out), .Q(PC_q), .clk(uc_1_pc), .clr(uc_1_rst_pc));  // open: carry
  UC uc_1 (
    .Clock(clock_1_out), .reset(button_1_out), .rst_PC(uc_1_rst_pc), .Dados(uc_1_dados),
    .Operando(uc_1_operando), .E(uc_1_e), .opcode(uc_1_opcode), .\Instrução (ir_1_s), .IR(uc_1_ir),
    .PC(uc_1_pc), .AC(uc_1_ac), .RAM(uc_1_ram), .O(d_ff_1_q), .Z(d_ff_2_q), .LOAD(uc_1_load), .RW(uc_1_rw),
    .D(uc_1_e));
  Clock clock_1 (.out(clock_1_out));
  Button button_1 (.out(button_1_out));
  ROM #(.addrWidth(4)) rom_1 (.addr(PC_q), .data(rom_1_data));  // open: sel
  IR ir_1 (.clock(uc_1_ir), .S(ir_1_s), .E(rom_1_data));
  Mux mux_1 (.E(uc_1_operando), .C(uc_1_e), .D(ram_1_data), .S(mux_1_s));
  ULA ula_1 (
    .D(uc_1_e), .B(mux_1_s), .A(ac_1_s), .in_4(uc_1_opcode), .S(ula_1_s), .Zero(ula_1_zero),
    .Overflow(ula_1_overflow));
  AC ac_1 (.Clock(uc_1_ac), .E(ula_1_s), .S(ac_1_s));
  D_Flip_Flop d_ff_1 (.clk(uc_1_ac), .D(ula_1_overflow), .Q(d_ff_1_q));  // open: Qn, preset, en, reset
  D_Flip_Flop d_ff_2 (.clk(uc_1_ac), .D(ula_1_zero), .Q(d_ff_2_q));  // open: Qn, preset, en, reset
  RAM #(.addrWidth(4), .dataWidth(4)) ram_1 (
    .addr(uc_1_operando), .data(ram_1_data), .clk(uc_1_ram), .ld(uc_1_rw));  // open: sel, clr
  Buffer buffer_1 (.S(ram_1_data), .in_2(not_2_out), .E(ac_1_s));
  not not_2 (not_2_out, uc_1_rw);

  // Notes on the sheet:
  //   contents of rom_1 (hex, n*v repeats v):
  //   1 21
endmodule

module add_1 (
  input  A,
  input  B,
  input  C,
  output S,
  output Vai_1
);

  wire and_1_out, and_2_out, or_1_out, xor_1_out;

  xor xor_1 (xor_1_out, C, B);
  or or_1 (or_1_out, C, B);
  and and_1 (and_1_out, or_1_out, A);
  and and_2 (and_2_out, C, B);
  xor xor_2 (S, xor_1_out, A);
  or or_2 (Vai_1, and_1_out, and_2_out);
endmodule

module Add_4 (
  input  [3:0] B,
  input  [3:0] A,
  output Overflow,
  output [3:0] S
);

  wire add_1_2_vai_1, add_1_3_vai_1, add_1_4_vai_1;

  add_1 add_1_1 (.S(S[3]), .Vai_1(Overflow), .A(A[3]), .B(B[3]), .C(add_1_2_vai_1));
  add_1 add_1_2 (.S(S[2]), .Vai_1(add_1_2_vai_1), .A(A[2]), .B(B[2]), .C(add_1_3_vai_1));
  add_1 add_1_3 (.S(S[1]), .Vai_1(add_1_3_vai_1), .A(A[1]), .B(B[1]), .C(add_1_4_vai_1));
  add_1 add_1_4 (.S(S[0]), .Vai_1(add_1_4_vai_1), .A(A[0]), .B(B[0]), .C(1'b0));
endmodule

module Sub_1 (
  input  A,
  input  B,
  input  C,
  output S,
  output Vai_1
);

  wire and_1_out, and_2_out, or_1_out, xor_1_out;

  xor xor_1 (xor_1_out, C, B);
  or or_1 (or_1_out, C, B);
  and and_1 (and_1_out, or_1_out, ~A);  // AND_Gate
  and and_2 (and_2_out, C, B);
  xor xor_2 (S, xor_1_out, A);
  or or_2 (Vai_1, and_1_out, and_2_out);
endmodule

module Sub_4 (
  input  [3:0] B,
  input  [3:0] in_2,
  output out_3,
  output [3:0] out_4
);

  wire sub_1_2_vai_1, sub_1_3_vai_1, sub_1_4_vai_1;

  Sub_1 sub_1_1 (.S(out_4[3]), .Vai_1(out_3), .A(in_2[3]), .B(B[3]), .C(sub_1_2_vai_1));
  Sub_1 sub_1_2 (.S(out_4[2]), .Vai_1(sub_1_2_vai_1), .A(in_2[2]), .B(B[2]), .C(sub_1_4_vai_1));
  Sub_1 sub_1_3 (.S(out_4[0]), .Vai_1(sub_1_3_vai_1), .A(in_2[0]), .B(B[0]), .C(1'b0));
  Sub_1 sub_1_4 (.S(out_4[1]), .Vai_1(sub_1_4_vai_1), .A(in_2[1]), .B(B[1]), .C(sub_1_3_vai_1));
endmodule

module Rot_esq (
  input  [3:0] abcd,
  input  [1:0] XY,
  output [3:0] out_3
);

  wire and_1_out, and_2_out, and_3_out, and_4_out, and_5_out, and_6_out, and_7_out, and_8_out, and_9_out;

  and and_1 (and_1_out, ~XY[1], ~XY[0], abcd[3]);  // AND_Gate
  and and_2 (and_2_out, ~XY[1], XY[0], abcd[2]);  // AND_Gate
  and and_3 (and_3_out, XY[1], ~XY[0], abcd[1]);  // AND_Gate
  and and_4 (and_4_out, XY[1], XY[0], abcd[0]);
  and and_5 (and_5_out, ~XY[1], ~XY[0], abcd[2]);  // AND_Gate
  and and_6 (and_6_out, ~XY[1], XY[0], abcd[1]);  // AND_Gate
  and and_7 (and_7_out, XY[1], ~XY[0], abcd[0]);  // AND_Gate
  and and_8 (and_8_out, ~XY[1], ~XY[0], abcd[1]);  // AND_Gate
  and and_9 (and_9_out, ~XY[1], XY[0], abcd[0]);  // AND_Gate
  and and_10 (out_3[0], ~XY[1], ~XY[0], abcd[0]);  // AND_Gate
  or or_1 (out_3[3], and_1_out, and_2_out, and_3_out, and_4_out);
  or or_2 (out_3[2], and_5_out, and_6_out, and_7_out);
  or or_3 (out_3[1], and_8_out, and_9_out);
endmodule

module Rot_dir (
  input  [3:0] abcd,
  input  [1:0] xy,
  output [3:0] ABCD_2
);

  wire and_1_out, and_2_out, and_3_out, and_4_out, and_5_out, and_6_out, and_7_out, and_8_out, and_9_out;

  and and_1 (and_1_out, ~xy[1], ~xy[0], abcd[0]);  // AND_Gate
  and and_2 (and_2_out, ~xy[1], xy[0], abcd[1]);  // AND_Gate
  and and_3 (and_3_out, xy[1], ~xy[0], abcd[2]);  // AND_Gate
  and and_4 (and_4_out, xy[1], xy[0], abcd[3]);
  and and_5 (and_5_out, ~xy[1], ~xy[0], abcd[1]);  // AND_Gate
  and and_6 (and_6_out, ~xy[1], xy[0], abcd[2]);  // AND_Gate
  and and_7 (and_7_out, xy[1], ~xy[0], abcd[3]);  // AND_Gate
  and and_8 (and_8_out, ~xy[1], ~xy[0], abcd[2]);  // AND_Gate
  and and_9 (and_9_out, ~xy[1], xy[0], abcd[3]);  // AND_Gate
  and and_10 (ABCD_2[3], ~xy[1], ~xy[0], abcd[3]);  // AND_Gate
  or or_1 (ABCD_2[0], and_1_out, and_2_out, and_3_out, and_4_out);
  or or_2 (ABCD_2[1], and_5_out, and_6_out, and_7_out);
  or or_3 (ABCD_2[2], and_8_out, and_9_out);
endmodule

module Dec_3x8 (
  input  [2:0] in_1,
  output S1,
  output S2,
  output S3,
  output S4,
  output S5,
  output S6,
  output S7,
  output S7_2
);

  wire not_1_out, not_2_out, not_3_out, not_4_out, not_5_out, not_6_out, not_7_out, not_8_out, not_9_out,
       not_10_out, not_11_out, not_12_out;

  not not_1 (not_1_out, in_1[2]);
  not not_2 (not_2_out, in_1[1]);
  not not_3 (not_3_out, in_1[0]);
  not not_4 (not_4_out, in_1[2]);
  not not_5 (not_5_out, in_1[1]);
  not not_6 (not_6_out, in_1[2]);
  not not_7 (not_7_out, in_1[0]);
  not not_8 (not_8_out, in_1[2]);
  not not_9 (not_9_out, in_1[1]);
  not not_10 (not_10_out, in_1[0]);
  not not_11 (not_11_out, in_1[1]);
  not not_12 (not_12_out, in_1[0]);
  and and_1 (S7_2, in_1[2], in_1[1], in_1[0]);
  and and_2 (S1, not_1_out, not_2_out, not_3_out);
  and and_3 (S2, not_4_out, not_5_out, in_1[0]);
  and and_4 (S3, not_6_out, in_1[1], not_7_out);
  and and_5 (S4, not_8_out, in_1[1], in_1[0]);
  and and_6 (S5, in_1[2], not_9_out, not_10_out);
  and and_7 (S6, in_1[2], not_11_out, in_1[0]);
  and and_8 (S7, in_1[2], in_1[1], not_12_out);
endmodule

module Buffer (
  input  [3:0] E,
  input  in_2,
  output [3:0] S
);

  assign S[3] = in_2 ? E[3] : 1'bz;  // Controlled_Buffer controlled_buffer_1
  assign S[0] = in_2 ? E[0] : 1'bz;  // Controlled_Buffer controlled_buffer_2
  assign S[2] = in_2 ? E[2] : 1'bz;  // Controlled_Buffer controlled_buffer_3
  assign S[1] = in_2 ? E[1] : 1'bz;  // Controlled_Buffer controlled_buffer_4
endmodule

module Or_4bits (
  input  [3:0] B,
  input  [3:0] A,
  output [3:0] S
);

  or or_1 (S[3], A[3], B[3]);
  or or_2 (S[2], A[2], B[2]);
  or or_3 (S[1], A[1], B[1]);
  or or_4 (S[0], A[0], B[0]);
endmodule

module Not_4 (
  input  [3:0] E,
  output [3:0] S
);

  not not_1 (S[2], E[2]);
  not not_2 (S[3], E[3]);
  not not_3 (S[0], E[0]);
  not not_4 (S[1], E[1]);
endmodule

module ULA (
  input  D,
  input  [3:0] B,
  input  [3:0] A,
  input  [2:0] in_4,
  output Overflow,
  output [3:0] S,
  output Zero
);

  wire add_4_1_overflow, and_1_out, and_2_out, dec_3x8_1_s1, dec_3x8_1_s2, dec_3x8_1_s3, dec_3x8_1_s4,
       dec_3x8_1_s5, dec_3x8_1_s6, dec_3x8_1_s7, dec_3x8_1_s7_2, not_1_out, sub_4_1_out_3;
  wire [3:0] add_4_1_s, buffer_7_s, not_4_1_s, or_4bits_1_s, rot_dir_1_abcd_2, rot_esq_1_out_3, sub_4_1_out_4;

  and and_1 (and_1_out, add_4_1_overflow, dec_3x8_1_s2);
  or or_1 (Overflow, and_1_out, and_2_out);
  and and_2 (and_2_out, sub_4_1_out_3, dec_3x8_1_s3);
  Dec_3x8 dec_3x8_1 (
    .in_1(in_4), .S1(dec_3x8_1_s1), .S2(dec_3x8_1_s2), .S3(dec_3x8_1_s3), .S4(dec_3x8_1_s4),
    .S5(dec_3x8_1_s5), .S6(dec_3x8_1_s6), .S7(dec_3x8_1_s7), .S7_2(dec_3x8_1_s7_2));
  Add_4 add_4_1 (.Overflow(add_4_1_overflow), .S(add_4_1_s), .A(A), .B(B));
  Buffer buffer_1 (.S(S), .in_2(dec_3x8_1_s2), .E(add_4_1_s));
  Buffer buffer_2 (.S(S), .in_2(dec_3x8_1_s1), .E(B));
  Sub_4 sub_4_1 (.out_3(sub_4_1_out_3), .B(B), .in_2(A), .out_4(sub_4_1_out_4));
  Buffer buffer_3 (.S(S), .in_2(dec_3x8_1_s3), .E(sub_4_1_out_4));
  Or_4bits or_4bits_1 (.A(A), .B(B), .S(or_4bits_1_s));
  Buffer buffer_4 (.S(S), .in_2(dec_3x8_1_s4), .E(or_4bits_1_s));
  nor nor_1 (Zero, S[0], S[1], S[2], S[3], dec_3x8_1_s7, dec_3x8_1_s7_2);
  Not_4 not_4_1 (.E(B), .S(not_4_1_s));
  Buffer buffer_5 (.S(S), .in_2(dec_3x8_1_s5), .E(not_4_1_s));
  Rot_esq rot_esq_1 (.abcd(A), .XY(B[1:0]), .out_3(rot_esq_1_out_3));
  Rot_dir rot_dir_1 (.abcd(A), .xy(B[1:0]), .ABCD_2(rot_dir_1_abcd_2));
  Buffer buffer_6 (.S(S), .in_2(dec_3x8_1_s6), .E(buffer_7_s));
  not not_1 (not_1_out, D);
  Buffer buffer_7 (.S(buffer_7_s), .in_2(not_1_out), .E(rot_esq_1_out_3));
  Buffer buffer_8 (.S(buffer_7_s), .in_2(D), .E(rot_dir_1_abcd_2));
endmodule

module AC (
  input  Clock,
  input  [3:0] E,
  output [3:0] S
);

  D_Flip_Flop d_ff_1 (.clk(Clock), .D(E[3]), .Q(S[3]));  // open: Qn, preset, en, reset
  D_Flip_Flop d_ff_2 (.clk(Clock), .D(E[2]), .Q(S[2]));  // open: Qn, preset, en, reset
  D_Flip_Flop d_ff_3 (.clk(Clock), .D(E[1]), .Q(S[1]));  // open: Qn, preset, en, reset
  D_Flip_Flop d_ff_4 (.clk(Clock), .D(E[0]), .Q(S[0]));  // open: Qn, preset, en, reset
endmodule

module Mux (
  input  [3:0] E,
  input  [3:0] D,
  input  C,
  output [3:0] S
);

  wire not_1_out;

  not not_1 (not_1_out, C);
  Buffer buffer_1 (.S(S), .in_2(not_1_out), .E(E));
  Buffer buffer_2 (.S(S), .in_2(C), .E(D));
endmodule

module IR (
  input  clock,
  input  [7:0] E,
  output [7:0] S
);

  D_Flip_Flop d_ff_1 (.clk(clock), .D(E[7]), .Q(S[7]));  // open: Qn, preset, en, reset
  D_Flip_Flop d_ff_2 (.clk(clock), .D(E[6]), .Q(S[6]));  // open: Qn, preset, en, reset
  D_Flip_Flop d_ff_3 (.clk(clock), .D(E[5]), .Q(S[5]));  // open: Qn, preset, en, reset
  D_Flip_Flop d_ff_4 (.clk(clock), .D(E[4]), .Q(S[4]));  // open: Qn, preset, en, reset
  D_Flip_Flop d_ff_5 (.clk(clock), .D(E[3]), .Q(S[3]));  // open: Qn, preset, en, reset
  D_Flip_Flop d_ff_6 (.clk(clock), .D(E[2]), .Q(S[2]));  // open: Qn, preset, en, reset
  D_Flip_Flop d_ff_7 (.clk(clock), .D(E[1]), .Q(S[1]));  // open: Qn, preset, en, reset
  D_Flip_Flop d_ff_8 (.clk(clock), .D(E[0]), .Q(S[0]));  // open: Qn, preset, en, reset
endmodule

module UC (
  input  [7:0] \Instrução ,
  input  Clock,
  input  reset,
  input  O,
  input  Z,
  output [3:0] Dados,
  output [3:0] Operando,
  output IR,
  output PC,
  output AC,
  output RAM,
  output rst_PC,
  output E,
  output [2:0] opcode,
  output D,
  output LOAD,
  output RW
);

  wire and_3_out, and_6_out, and_7_out, nand_1_out;
  wire [1:0] counter_1_q;

  Counter #(.width(2), .max('h3)) counter_1 (.Q(counter_1_q), .clk(Clock), .clr(reset));  // open: load, D, count, carry
  nand STOR (RW, AC, \Instrução [7], \Instrução [6], \Instrução [5], \Instrução [4]);
  and and_1 (IR, ~counter_1_q[1], ~counter_1_q[0]);  // AND_Gate
  and and_2 (PC, ~counter_1_q[1], counter_1_q[0]);  // AND_Gate
  and and_3 (and_3_out, \Instrução [7], \Instrução [6], ~\Instrução [5], \Instrução [4], PC, O);  // AND_Gate
  and and_4 (AC, counter_1_q[1], ~counter_1_q[0]);  // AND_Gate
  and and_5 (RAM, counter_1_q[1], counter_1_q[0]);
  and and_6 (and_6_out, \Instrução [7], \Instrução [6], ~\Instrução [5], ~\Instrução [4], PC, Z);  // AND_Gate
  and and_7 (and_7_out, \Instrução [7], \Instrução [6], \Instrução [5], ~\Instrução [4], PC);  // AND_Gate
  or or_1 (LOAD, and_7_out, and_6_out, and_3_out);
  nand nand_1 (nand_1_out, \Instrução [7], ~\Instrução [6], \Instrução [5]);  // NAND_Gate
  and and_8 (D, \Instrução [4], nand_1_out);

  assign Dados = \Instrução [3:0];
  assign E = \Instrução [4];
  assign opcode = \Instrução [7:5];
  assign Operando = \Instrução [3:0];
  assign rst_PC = reset;

  // Notes on the sheet:
  //   jpo
  //   jpz
  //   goto
endmodule
